# Fritzing sketch ziot-station01 (saved by Fritzing 0.9.3b)
circuit board: 8.47cm x 5.64444cm
breadboards: 1

parts:
  ESP8266_NodeMCU_1_0 = NodeMCU V1.0
  R3 = Resistor [tolerance=±5% resistance=220 package=THT]
  R2 = Resistor [tolerance=±5% resistance=220 package=THT]
  R4 = Resistor [tolerance=±5% resistance=220 package=THT]
  R5 = Resistor [tolerance=±5% resistance=220 package=THT]
  LED1 = LED - 5mm [color="Red (633nm)" package="5 mm [THT]"]
  S1 = Toggle Switch [package=THT]
  R1 = Resistor [tolerance=±5% resistance=220 package=THT]
  S2 = Toggle Switch [package=THT]
  R6 = Resistor [tolerance=±5% resistance=1k package=THT]
  R7 = Resistor [tolerance=±20% resistance=1k package=THT]
  SN74HCT00N = SN74LS32N [package="DIP14 [THT]"]
  OLED_SSD_1306 = male pin header, 4 pins [form="♂ (male)"]
  DHT22_IN = male pin header, 3 pins [form="♂ (male)"]
  DHT22_OUT = male pin header, 3 pins [form="♂ (male)"]
  Micro_USB = Adafruit Micro USB Breakout [part_number="Adafruit #1833"]

nets:
  N1: ESP8266_NodeMCU_1_0.D1, R4.Pin_1, DHT22_OUT.pin1
  N2: ESP8266_NodeMCU_1_0.D2, R2.Pin_1, DHT22_IN.pin1
  N3: ESP8266_NodeMCU_1_0.D3, SN74HCT00N.1A, SN74HCT00N.2Y
  N4: ESP8266_NodeMCU_1_0.3V3, OLED_SSD_1306.pin2
  GND: ESP8266_NodeMCU_1_0.GND, LED1.cathode, S2.COM, SN74HCT00N.GND, OLED_SSD_1306.pin1, DHT22_IN.pin3, DHT22_OUT.pin3, Micro_USB.GND
  N5: ESP8266_NodeMCU_1_0.D5, OLED_SSD_1306.pin3
  N6: ESP8266_NodeMCU_1_0.D6, OLED_SSD_1306.pin4
  VIN: ESP8266_NodeMCU_1_0.Vin, R3.Pin_1, R5.Pin_1, S1.L2, R1.Pin_1, R6.Pin_1, R7.Pin_1, SN74HCT00N.Vcc, DHT22_IN.pin2, DHT22_OUT.pin2
  N7: R3.Pin_0, R2.Pin_0
  N8: R4.Pin_0, R5.Pin_0
  N9: LED1.anode, R1.Pin_0
  N10: S1.COM, Micro_USB.VBUS
  N11: S2.L1, R6.Pin_0, SN74HCT00N.1B
  N12: S2.L2, R7.Pin_0, SN74HCT00N.2B
  N13: SN74HCT00N.1Y, SN74HCT00N.2A

notes:
  Vcc
  GND
  3V3
  D6
  D5
  D1
  D2
  D3
  CLK
  SDA

custom parts:
  NodeMCU V1.0: ESP8266 based NodeMCU
  Adafruit Micro USB Breakout: Simple but effective - this breakout board has a USB Micro-B connector, with all 5 pins broken out. Great for pairing with a microcontroller with USB support, or adding USB 5V power to a project. We use a micro-AB connector with through-hole shielding pads for an excellent strong connection - it won't rip off by accident! Comes with one fully assembled and tested micro B breakout PCB and a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
